# Fritzing sketch gateOpener (saved by Fritzing 0.9.3b)

parts:
  Componente1 = RFID-RC522-v2
  Componente2 = Arduino Uno (Rev3)
  Grove1 = Grove OLED 128x96
  Matrix_keypad1 = KEYPAD 4x4
  U1 = RELAY [package=relay-g5q]
  R1 = Resistor [tolerance=±5% resistance=220 package="2512 [SMD]"]

nets:
  N1: Componente1.SDA, Componente2.D10_PWM/SS
  N2: Componente1.SCK, Componente2.D13/SCK
  N3: Componente1.MOSI, Componente2.D11_PWM/MOSI
  N4: Componente1.MISO, Componente2.D12/MISO
  GND: Componente1.GND, Componente2.GND, Grove1.GND, U1.COIL2
  N5: Componente1.RST, Componente2.D9_PWM
  3.3V: Componente1.3.3V, Componente2.3V3
  N6: Componente2.A0, Matrix_keypad1.row4
  N7: Componente2.A1, R1.Pin_1
  N8: Componente2.A4/SDA, Grove1.SDA
  N9: Componente2.A5/SCL, Grove1.SCL
  N10: Componente2.D8, Matrix_keypad1.col1
  N11: Componente2.D2, Matrix_keypad1.row3
  N12: Componente2.D3_PWM, Matrix_keypad1.row2
  N13: Componente2.D4, Matrix_keypad1.row1
  N14: Componente2.D5_PWM, Matrix_keypad1.col4
  N15: Componente2.D6_PWM, Matrix_keypad1.col3
  N16: Componente2.D7, Matrix_keypad1.col2
  5V: Componente2.5V, Grove1.VCC

custom parts:
  RFID-RC522-v2: A simple China made RFID-RC522 Reader; do check the pin labels, as this is a MFRC522 based clone.
  KEYPAD 4x4: Matrix keypad 16 buttons, 4 rows x 4 columns
